# Fritzing sketch eletrico-carrinho (saved by Fritzing 1.0.1rc)
breadboards: 1

parts:
  Componente1 = Arduino Uno (Rev3)
  L298N1 = L298N DC motor driver
  M1 = Getriebemotor
  M2 = Getriebemotor
  M3 = fc-51 [package=THT]  # not connected
  M4 = fc-51 [package=THT]  # not connected
  M5 = fc-51 [package=THT]  # not connected
  Componente2 = SRF05 Ultrasonic Rangefinder  # not connected
  Componente3 = RFID-RC522-v2
  U1 = LCD-16X2 [package=lcd-16x2]
  LCM1602_IIC1 = LCM1602 IIC [part_number="LCM1602 IIC" chip_label="LCM1602 IIC" package="DIP (Dual Inline) [THT]"]
  M6 = Getriebemotor
  M7 = Getriebemotor

nets:
  N1: Componente1.A4/SDA, LCM1602_IIC1.SDA
  N2: Componente1.A5/SCL, LCM1602_IIC1.SCL
  N3: Componente1.D9_PWM, Componente3.RST
  N4: Componente1.D10_PWM/SS, Componente3.SDA
  N5: Componente1.D11_PWM/MOSI, Componente3.MOSI
  N6: Componente1.D12/MISO, Componente3.MISO
  N7: Componente1.D13/SCK, Componente3.SCK
  N8: Componente1.D0/RX, L298N1.IN3
  N9: Componente1.D1/TX, L298N1.IN1
  N10: Componente1.D2, L298N1.IN4
  N11: Componente1.D4, L298N1.IN2
  N12: Componente1.D5_PWM, L298N1.ENB
  N13: Componente1.D6_PWM, L298N1.ENA
  5V: Componente1.5V, Componente3.3.3V, LCM1602_IIC1.VCC
  GND: Componente1.GND, L298N1.GND, Componente3.GND, LCM1602_IIC1.GND
  VIN: Componente1.VIN, L298N1.12V
  N14: L298N1.OUT1, M2.pin_2, M6.pin_1
  N15: L298N1.OUT2, M2.pin_1, M6.pin_2
  N16: L298N1.OUT3, M1.pin_2, M7.pin_2
  N17: L298N1.OUT4, M1.pin_1, M7.pin_1
  VSS: U1.VSS, LCM1602_IIC1.VSS
  VDD: U1.VDD, LCM1602_IIC1.VDD
  N18: U1.VO, LCM1602_IIC1.V0
  N19: U1.RS, LCM1602_IIC1.RS
  N20: U1.R_W, LCM1602_IIC1.RW
  N21: U1.E, LCM1602_IIC1.E
  N22: U1.DB0, LCM1602_IIC1.D0
  N23: U1.DB1, LCM1602_IIC1.D1
  N24: U1.DB2, LCM1602_IIC1.D2
  N25: U1.DB3, LCM1602_IIC1.D3
  N26: U1.DB4, LCM1602_IIC1.D4
  N27: U1.DB5, LCM1602_IIC1.D5
  N28: U1.DB6, LCM1602_IIC1.D6
  N29: U1.DB7, LCM1602_IIC1.D7
  N30: U1.A, LCM1602_IIC1.A

custom parts:
  L298N DC motor driver: 2x DC motor driver with 78M05 positive voltage regulator (7..35 V) L298N: max 46 V, 2 A Set 5 V Enable jumper to enable 5 V regultor (needed for the L298N) and +5 V output at screw terminal or supply external +5 V at screw terminal Set ENA and/or ENB to +5 V to enable motor permanently or supply ENA and/or ENB with PWM signal IN1 and IN2 set rotation directory for motor A (OUT1/OUT2) IN2 and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
  RFID-RC522-v2: A simple China made RFID-RC522 Reader; do check the pin labels, as this is a MFRC522 based clone.
  LCM1602 IIC: I2C-Module to use a 1602 or 2004 LCD on with the wire.h libory Serial LCD Modul
